// Digital circuit 2bitmulti.dig as structural Verilog
module _2bitmulti (
  input  a1,
  input  a0,
  input  b1,
  input  b0,
  output p0,
  output p1,
  output p2,
  output p3
);

  wire and_1_out, and_2_out, and_4_out, and_5_out, and_6_out, and_7_out, not_1_out, not_2_out, not_3_out,
       not_4_out, not_5_out, not_6_out;

  not not_1 (not_1_out, a0);
  not not_2 (not_2_out, b0);
  and and_1 (and_1_out, a1, b1, not_1_out);
  and and_2 (and_2_out, a1, b1, not_2_out);
  and and_3 (p0, a1, b0);
  not not_3 (not_3_out, a1);
  not not_4 (not_4_out, b0);
  not not_5 (not_5_out, a0);
  not not_6 (not_6_out, b1);
  and and_4 (and_4_out, not_3_out, a0, b1);
  and and_5 (and_5_out, a0, b1, not_4_out);
  and and_6 (and_6_out, a1, not_5_out, b0);
  and and_7 (and_7_out, a1, not_6_out, b0);
  and and_8 (p3, a1, a0, b1, b0);
  or or_1 (p2, and_1_out, and_2_out);
  or or_2 (p1, and_4_out, and_5_out, and_6_out, and_7_out);
endmodule
