// Digital circuit fourbitadder.dig as structural Verilog
module fourbitadder (
  input  [3:0] A,
  input  [3:0] B,
  output [3:0] out_3
);

  wire onebit_1_p5, onebit_2_p5, onebit_3_p5, onebit_4_p5;

  // onebit onebit_1: pin names not known; wires that end beside it: A[0], B[0], 1'b0, out_3[0], onebit_1_p5
  // onebit onebit_2: pin names not known; wires that end beside it: A[1], B[1], onebit_1_p5, out_3[1], onebit_2_p5
  // onebit onebit_3: pin names not known; wires that end beside it: A[2], B[2], onebit_2_p5, out_3[2], onebit_3_p5
  // onebit onebit_4: pin names not known; wires that end beside it: A[3], B[3], onebit_3_p5, out_3[3], onebit_4_p5
  LED led_1 (.in(onebit_4_p5));
endmodule
